# Fritzing sketch led (saved by Fritzing 0.9.4)
breadboards: 1

parts:
  Part1 = Arduino Uno (Rev3)
  LED1 = LED - 5mm [color="Red (633nm)" package="5 mm [THT]"]
  LED2 = LED - 5mm [color="Red (633nm)" package="5 mm [THT]"]
  R1 = Resistor [tolerance=±5% resistance=220 package=THT]
  R2 = Resistor [tolerance=±5% resistance=220 package=THT]

nets:
  N1: Part1.D8, LED2.cathode
  N2: Part1.D13/SCK, LED1.cathode
  N3: Part1.GND, R1.Pin_1, R2.Pin_1
  N4: LED1.anode, R2.Pin_0
  N5: LED2.anode, R1.Pin_0
